// Digital circuit atk16.dig as structural Verilog
module atk16 (
  input  clk,
  input  IN,
  output OUT
);

  wire ALU_OE, atk16_decoder_1_p5, atk16_decoder_1_p7, FR_IE, IR_IE, JA_OE, MAR_IE, MEM_IE, MEM_OE,
       not_1_out, or_1_out, PC_CO, PC_IE, PC_OE, R1_OE, R2_OE, reset_1_out, RW_IE, US_RS;
  wire [2:0] FLAG_EQ, Microsequencer_out;
  wire [3:0] ALU_flags, atk16_decoder_1_p8, FR_q, OPCODE;
  wire [3:3] bitselector_1_out;
  wire [14:11] UCODE_d;
  wire [15:0] ALU_y, atk16_decoder_1_p1, atk16_regbank_1_p7, atk16_regbank_1_p8, MAR_q, PC_out;

  Break break_1 (.brk(clk));
  or or_1 (or_1_out, US_RS, reset_1_out);
  Reset #(.invertOutput("false")) reset_1 (.out(reset_1_out));
  CounterPreset #(.Bits(16), .isProgramCounter("true")) PC (
    .en(PC_CO), .C(clk), .dir(1'b0), .in(atk16_decoder_1_p1), .ld(PC_IE), .clr(1'b0), .out(PC_out));  // open: ovf
  // atk16_decoder atk16_decoder_1: pin names not known; wires that end beside it: atk16_decoder_1_p1, IR_IE, clk, JA_OE, atk16_decoder_1_p5, FLAG_EQ, atk16_decoder_1_p7, atk16_decoder_1_p8, OPCODE
  // Probe OPCODE on OPCODE
  Counter #(.Bits(3)) Microsequencer (.en(1'b1), .C(not_1_out), .clr(or_1_out), .out(Microsequencer_out));  // open: ovf
  not not_1 (not_1_out, clk);
  assign atk16_decoder_1_p1 = PC_OE ? PC_out : 16'bz;  // Driver driver_1
  // Probe Bus on atk16_decoder_1_p1
  // atk16_regbank atk16_regbank_1: pin names not known; wires that end beside it: atk16_decoder_1_p1, RW_IE, atk16_decoder_1_p5, clk, FLAG_EQ, atk16_decoder_1_p7, atk16_regbank_1_p7, atk16_regbank_1_p8
  Register #(.Bits(4)) FR (.D(ALU_flags), .C(clk), .en(FR_IE), .Q(FR_q));
  Register #(.Bits(16)) MAR (.D(atk16_decoder_1_p1), .C(clk), .en(MAR_IE), .Q(MAR_q));
  assign atk16_decoder_1_p1 = R1_OE ? atk16_regbank_1_p7 : 16'bz;  // Driver driver_2
  BitSelector #(.Selector_Bits(2)) bitselector_1 (.in(FR_q), .sel(FLAG_EQ[1:0]), .out(bitselector_1_out[3]));
  assign atk16_decoder_1_p1 = R2_OE ? atk16_regbank_1_p8 : 16'bz;  // Driver driver_3
  atk16_alu ALU (.A(atk16_regbank_1_p7), .B(atk16_regbank_1_p8), .S(atk16_decoder_1_p8), .Y(ALU_y), .FLAGS(ALU_flags));
  atk16_mem atk16_mem_1 (
    .ADDR(MAR_q), .DBUS(atk16_decoder_1_p1), .CLK(MEM_IE), .MEM_IE(MEM_OE));  // open: MEM_OE, MMIO_IE, MMIO_OE, MMIO_S
  assign atk16_decoder_1_p1 = ALU_OE ? ALU_y : 16'bz;  // Driver driver_4
  EEPROM #(.AddrBits(8), .Bits(16)) UCODE (
    .A({OPCODE, bitselector_1_out[3], Microsequencer_out}), .CS(1'b1), .WE(1'b0), .OE(1'b1),
    .D({US_RS, UCODE_d[14], FR_IE, ALU_OE, UCODE_d[11], JA_OE, IR_IE, R2_OE, R1_OE, RW_IE, MEM_OE, MEM_IE, MAR_IE, PC_OE, PC_IE, PC_CO}));
  // Probe ALU on ALU_y
  Stop stop_1 (.stop(UCODE_d[14]));

  assign OUT = 1'b0;
  // also tied to GND on the sheet: IN

  // Notes on the sheet:
  //   clk: Hz: 10
  //   OUT: Dummy output
  //   contents of UCODE (hex, n*v repeats v):
  //   c,221,3040,8000,4*0,c,221,3040,8000,4*0,c,221,3040,8000,4*0,c
  //   ,221,3040,8000,4*0,c,221,88,60,8000,0,0,0,c,221,88,60,8000,0,0,0
  //   ,c,221,88,110,8000,0,0,0,c,221,88,110,8000,0,0,0,c,221,440,8000
  //   ,4*0,c,221,440,8000,4*0,c,221,82,8000,4*0,c,221,82,8000,4*0,c
  //   ,221,8000,5*0,c,221,102,8000,4*0,c,221,8000,5*0,c,221,8000,5*0
  //   ,c,221,8000,5*0,c,221,8000,5*0,c,221,8000,5*0,c,221,8000,5*0,c
  //   ,221,8000,5*0,c,221,8000,5*0,c,221,8000,5*0,c,221,8000,5*0,c,221
  //   ,8000,5*0,c,221,8000,5*0,c,221,8000,5*0,c,221,8000,5*0,c,221,8000
  //   ,5*0,c,221,8000,5*0,c,221,4000,5*0,c,221,4000
endmodule

/* Test case Sum program TODO:
IN OUT

program(0x4051, 0x40a2, 0x029b)

0 x
*/
